# Fritzing sketch DisennoReleCarro (saved by Fritzing 0.9.3b)
breadboards: 1

parts:
  Componente1 = Arduino Uno (Rev3)
  Power_plug1 = Power plug
  Componente2 = Logic Level Converter
  J1 = female pin header, 4 pins [form="♀ (female)"]
  J2 = female pin header, 3 pins [form="♀ (female)"]

nets:
  N1: Componente1.D13/SCK, J2.pin3
  N2: Componente1.D4, Componente2.TX_HV
  N3: Componente1.D5_PWM, Componente2.RX_HV
  N4: Componente1.3V3, Componente2.LV
  N5: Componente1.5V, Componente2.HV, J1.pin4, J2.pin1
  GND: Componente1.GND, Power_plug1.GND, Componente2.GND, J1.pin3, J2.pin2
  VIN: Componente1.VIN, Power_plug1.VCC
  N6: Componente2.RX_LV, J1.pin2
  N7: Componente2.TX_LV, J1.pin1

notes:
  Negro - TX
  Rojo - RT
  Azul - GND
  Amarillo - 5Vcc
  5Vcc
  GND
  Senal
