# Fritzing sketch Diagrama Detector Temperatura (saved by Fritzing 0.9.3b)
breadboards: 1

parts:
  Componente1 = Arduino Uno (Rev3)
  LCD1 = LCD screen
  U1 = TMP36 [package=to-92-kit]
  S1 = Pushbutton [package="[THT]"]
  R1 = Rotary Potentiometer (Small) [maximum_resistance=100kΩ package=THT]
  R2 = Resistor [tolerance=±5% resistance=220 package=THT]
  J1 = female pin header, 3 pins [form="♀ (female)"]

nets:
  N1: Componente1.A0, U1.VOUT
  N2: Componente1.D8, S1.Pin_3, S1.Pin_4, R2.Pin_1
  N3: Componente1.D11_PWM/MOSI, LCD1.E
  N4: Componente1.D12/MISO, LCD1.RS
  N5: Componente1.D13/SCK, J1.pin1
  N6: Componente1.D2, LCD1.DB7
  N7: Componente1.D3_PWM, LCD1.DB6
  N8: Componente1.D4, LCD1.DB5
  N9: Componente1.D5_PWM, LCD1.DB4
  5V: Componente1.5V, LCD1.VDD, LCD1.LED+, U1.VCC, S1.Pin_1, S1.Pin_2, R1.leg2, J1.pin3
  GND: Componente1.GND, LCD1.VSS, LCD1.R/W, LCD1.LED-, U1.GND, R1.leg1, R2.Pin_0, J1.pin2
  N10: LCD1.V0, R1.wiper

notes:
  IN
  GND
  VCC
