# Fritzing sketch Diagrama (saved by Fritzing 0.9.3b)
breadboards: 1

parts:
  Componente1 = Arduino Uno (Rev3)
  R1 = Resistor [tolerance=±5% resistance=220 package=THT]
  S1 = Pushbutton [package="[THT]"]
  J1 = female pin header, 6 pins [form="♀ (female)"]

nets:
  N1: Componente1.D9_PWM, J1.pin4
  N2: Componente1.D10_PWM/SS, J1.pin3
  N3: Componente1.D11_PWM/MOSI, J1.pin2
  N4: Componente1.D12/MISO, J1.pin1
  N5: Componente1.GND, S1.Pin_1, S1.Pin_2, J1.pin5
  N6: Componente1.D2, R1.Pin_0
  N7: Componente1.D4, R1.Pin_1
  N8: Componente1.D6_PWM, S1.Pin_3, S1.Pin_4
  N9: Componente1.5V, J1.pin6

notes:
  Freno
  Intermitente
  Camburador
  direcion
